# Fritzing sketch attiny_pcb (saved by Fritzing 0.9.3b)
circuit board: 3.80501cm x 5.53564cm
breadboards: 1

parts:
  U3 = attiny85 [package=dip]
  PIR2 = PIR sensor
  BAT1 = Battery Holders [package=battcon_245mm_pth]
  LED3 = smd LED [color="Red (633nm)" package="0603 [SMD]"]
  R1 = Resistor [tolerance=±5% resistance=220 package="2010 [SMD]"]

nets:
  N1: U3.Pin_4, PIR2.GND, BAT1.-, R1.Pin_0
  N2: U3.Pin_5, LED3.anode
  N3: U3.Pin_7, PIR2.SIG
  N4: U3.Pin_8, PIR2.VDD, BAT1.+
  N5: LED3.cathode, R1.Pin_1
